// Logisim project SAP-1 Main.circ as structural Verilog: 3 circuits, main circuit main
module main (
  input  in_1,
  input  CLK_A_M,
  input  [7:0] in_3,
  input  in_4,
  input  in_5,
  input  in_6,
  input  in_7,
  input  in_8,
  input  in_9
);

  wire CLK, CLK_ADV_out, clock_1_out, CLR, HLT, multiplexer_1_out, not_1_out;
  wire [3:0] counter_1_q, n8_bit_bin2bcd_1_qh, n8_bit_bin2bcd_1_qo, n8_bit_bin2bcd_1_qt, register_1_q;
  wire [7:0] ram_1_data, register_2_q;

  Button CLK_ADV (.out(CLK_ADV_out));
  Pull_Resistor pull_resistor_1 (.node(HLT));
  Button RESET (.out(CLR));
  Clock clock_1 (.out(clock_1_out));
  Multiplexer #(.disabled(0), .enable("false")) multiplexer_1 (
    .in0(CLK_ADV_out), .in1(clock_1_out), .out(multiplexer_1_out), .sel(CLK_A_M));
  not not_1 (not_1_out, HLT);
  and and_1 (CLK, multiplexer_1_out, not_1_out);
  DotMatrix #(.inputtype("row"), .matrixcols(4), .matrixrows(1), .dotshape("circle")) dotmatrix_1 (.row0(register_1_q));
  Register #(.width(4)) register_1 (.D(in_3[3:0]), .en(in_7), .Q(register_1_q), .clk(CLK), .clr(CLR));
  DotMatrix #(.inputtype("row"), .matrixcols(8), .matrixrows(1), .dotshape("circle")) dotmatrix_2 (.row0(in_3));
  DotMatrix #(.inputtype("row"), .matrixcols(8), .matrixrows(1), .dotshape("circle")) dotmatrix_3 (.row0(ram_1_data));
  RAM #(.addrWidth(4), .bus("separate")) ram_1 (
    .addr(register_1_q), .din(in_3), .data(ram_1_data), .str(in_8), .sel(1'b1), .clk(CLK), .ld(1'b1),
    .clr(1'b0));
  assign in_3 = in_9 ? ram_1_data : 8'bz;  // Controlled_Buffer controlled_buffer_1
  Pull_Resistor pull_resistor_2 (.node(in_3[0]));
  Pull_Resistor pull_resistor_3 (.node(in_3[1]));
  Pull_Resistor pull_resistor_4 (.node(in_3[2]));
  Pull_Resistor pull_resistor_5 (.node(in_3[3]));
  Pull_Resistor pull_resistor_6 (.node(in_3[4]));
  Pull_Resistor pull_resistor_7 (.node(in_3[5]));
  Pull_Resistor pull_resistor_8 (.node(in_3[6]));
  Pull_Resistor pull_resistor_9 (.node(in_3[7]));
  DotMatrix #(.inputtype("row"), .matrixcols(4), .matrixrows(1), .dotshape("circle")) dotmatrix_4 (.row0(counter_1_q));
  assign in_3[3:0] = in_1 ? counter_1_q : 4'bz;  // Controlled_Buffer controlled_buffer_2
  Counter #(.width(4), .max('hf)) counter_1 (
    .load(in_4), .D(in_3[3:0]), .count(in_5), .Q(counter_1_q), .clk(CLK), .clr(CLR));  // open: carry
  Register register_2 (.D(in_3), .en(in_6), .Q(register_2_q), .clk(CLK), .clr(CLR));
  _8_BIT_BIN2BCD u_8_bit_bin2bcd_1 (
    .D(register_2_q), .QH(n8_bit_bin2bcd_1_qh), .QT(n8_bit_bin2bcd_1_qt), .QO(n8_bit_bin2bcd_1_qo));
  Hex_Digit_Display hex_digit_display_1 (.value(n8_bit_bin2bcd_1_qt));  // open: dp
  Hex_Digit_Display hex_digit_display_2 (.value(n8_bit_bin2bcd_1_qh));  // open: dp
  Hex_Digit_Display hex_digit_display_3 (.value(n8_bit_bin2bcd_1_qo));  // open: dp

  // Other names for the same wires on the sheet: BUS[7:0] = in_3; CE = in_5; CO = in_1; JMP = in_4; MI = in_7;
  //   OI = in_6; RI = in_8; RO = in_9

  // Notes on the sheet:
  //   MAR
  //   DATA BUS
  //   RAM CONTENTS
  //   PC
  //   OUTPUT REGISTER
endmodule

module ADD_3 (
  input  A3,
  input  A2,
  input  A1,
  input  A0,
  output S3,
  output S2,
  output S1,
  output S0
);

  wire and_1_out, and_2_out, and_3_out, and_4_out, and_5_out, and_6_out, and_7_out, and_8_out, and_9_out,
       and_10_out, not_1_out, not_2_out, not_3_out, not_4_out, not_5_out, not_6_out, not_7_out, not_8_out;

  and and_1 (and_1_out, A2, A0);
  and and_2 (and_2_out, A2, A1);
  and and_3 (and_3_out, A2, not_1_out, not_2_out);
  not not_1 (not_1_out, A1);
  not not_2 (not_2_out, A0);
  and and_4 (and_4_out, A3, A0);
  not not_3 (not_3_out, A2);
  and and_5 (and_5_out, not_3_out, A1);
  and and_6 (and_6_out, A1, A0);
  and and_7 (and_7_out, A3, not_4_out);
  not not_4 (not_4_out, A0);
  not not_5 (not_5_out, A3);
  and and_8 (and_8_out, not_5_out, not_6_out, A0);
  not not_6 (not_6_out, A2);
  and and_9 (and_9_out, A2, A1, not_7_out);
  not not_7 (not_7_out, A0);
  and and_10 (and_10_out, A3, not_8_out);
  not not_8 (not_8_out, A0);
  or or_1 (S3, and_1_out, and_2_out, A3);
  or or_2 (S2, and_3_out, and_4_out);
  or or_3 (S1, and_5_out, and_6_out, and_7_out);
  or or_4 (S0, and_8_out, and_9_out, and_10_out);
endmodule

module _8_BIT_BIN2BCD (
  input  [7:0] D,
  output [3:0] QH,
  output [3:0] QT,
  output [3:0] QO
);

  wire add_3_1_s0, add_3_1_s1, add_3_1_s2, add_3_1_s3, add_3_2_s0, add_3_2_s1, add_3_2_s2, add_3_2_s3,
       add_3_3_s0, add_3_3_s1, add_3_3_s2, add_3_3_s3, add_3_4_s0, add_3_4_s1, add_3_4_s2, add_3_5_s0,
       add_3_5_s1, add_3_5_s2, add_3_5_s3;

  ADD_3 add_3_1 (
    .A3(1'b0), .A2(D[7]), .A1(D[6]), .A0(D[5]), .S3(add_3_1_s3), .S2(add_3_1_s2), .S1(add_3_1_s1),
    .S0(add_3_1_s0));
  ADD_3 add_3_2 (
    .A3(add_3_1_s2), .A2(add_3_1_s1), .A1(add_3_1_s0), .A0(D[4]), .S3(add_3_2_s3), .S2(add_3_2_s2),
    .S1(add_3_2_s1), .S0(add_3_2_s0));
  ADD_3 add_3_3 (
    .A3(add_3_2_s2), .A2(add_3_2_s1), .A1(add_3_2_s0), .A0(D[3]), .S3(add_3_3_s3), .S2(add_3_3_s2),
    .S1(add_3_3_s1), .S0(add_3_3_s0));
  ADD_3 add_3_4 (
    .A3(1'b0), .A2(add_3_1_s3), .A1(add_3_2_s3), .A0(add_3_3_s3), .S3(QH[1]), .S2(add_3_4_s2),
    .S1(add_3_4_s1), .S0(add_3_4_s0));
  ADD_3 add_3_5 (
    .A3(add_3_3_s2), .A2(add_3_3_s1), .A1(add_3_3_s0), .A0(D[2]), .S3(add_3_5_s3), .S2(add_3_5_s2),
    .S1(add_3_5_s1), .S0(add_3_5_s0));
  ADD_3 add_3_6 (
    .A3(add_3_4_s2), .A2(add_3_4_s1), .A1(add_3_4_s0), .A0(add_3_5_s3), .S3(QH[0]), .S2(QT[3]), .S1(QT[2]),
    .S0(QT[1]));
  ADD_3 add_3_7 (
    .A3(add_3_5_s2), .A2(add_3_5_s1), .A1(add_3_5_s0), .A0(D[1]), .S3(QT[0]), .S2(QO[3]), .S1(QO[2]),
    .S0(QO[1]));

  assign QH[3:2] = 2'b00;
  assign QO[0] = D[0];
endmodule
